# Fritzing sketch mobileBBshield_for_Mozzi (saved by Fritzing 0.8.3b)
circuit board: 6.88561cm x 5.36311cm
breadboards: 1

parts:
  R4 = Resistor [tolerance=±5% resistance=270 package=THT]
  R1 = Resistor [tolerance=±5% resistance=680 package=THT]
  R2 = Resistor [tolerance=±5% resistance=680 package=THT]
  C1 = Ceramic Capacitor [capacitance=220nF package="100 mil [THT, multilayer]"]
  R3 = Resistor [tolerance=±5% resistance=330 package=THT]
  C2 = Ceramic Capacitor [capacitance=220nF package="100 mil [THT, multilayer]"]
  C3 = Ceramic Capacitor [capacitance=1nF package="100 mil [THT, multilayer]"]
  C4 = Ceramic Capacitor [capacitance=100nF package="100 mil [THT, multilayer]"]
  Arduino1 = Arduino Uno (Rev3)
  out = akizuki 3.5mm Audio Jack [package=audio-jack-3.5mm]
  in = akizuki 3.5mm Audio Jack [package=audio-jack-3.5mm]

nets:
  N1: R4.Pin_0, Arduino1.D9_PWM
  N2: R4.Pin_1, R1.Pin_0, C2.0, C4.0
  N3: R1.Pin_1, R2.Pin_0, C1.0
  N4: R2.Pin_1, C3.1, out.LEFT
  GND: C1.1, R3.Pin_1, C4.1, Arduino1.GND, out.SLEEVE, in.SLEEVE
  N5: R3.Pin_0, C2.1, C3.0
  N6: Arduino1.A0, in.LEFT

notes:
  in
  out
  audio
  mono audio output 3.5mm jack
  mono audio input 3.5mm jack
  D9 is default Mozzi output
  A0 is default Mozzi input
  D9 is default Mozzi output
  A0 is default Mozzi input
  6kHz low-pass and 16384Hz notch filter
  This circuit based on
  Notch filter for STANDARD mode carrier frequency
  (http://sensorium.github.io/Mozzi/learn/output/)
  input
  output

custom parts:
  akizuki 3.5mm Audio Jack: 3.5mm Audio Jack akizuki st-005

// code stored in the sketch: Blink.ino
/*
  Blink
  Turns on an LED on for one second, then off for one second, repeatedly.
 
  This example code is in the public domain.
 */

void setup() {                
  // initialize the digital pin as an output.
  // Pin 13 has an LED connected on most Arduino boards:
  pinMode(13, OUTPUT);     
}

void loop() {
  digitalWrite(13, HIGH);   // set the LED on
  delay(1000);              // wait for a second
  digitalWrite(13, LOW);    // set the LED off
  delay(1000);              // wait for a second
}
