# Fritzing sketch mobileBBshield_for_Mozzi_2014_mft (saved by Fritzing 0.9.0b)
circuit board: 10.2755cm x 5.35018cm
breadboards: 2

parts:
  R6 = Resistor [tolerance=±1% resistance=100k package="0603 [SMD]"]
  R5 = Resistor [tolerance=±1% resistance=100k package="0603 [SMD]"]
  C5 = Ceramic Capacitor [capacitance=47nF package="0603 [SMD, multilayer]"]
  R4 = Resistor [tolerance=±1% resistance=270 package="0603 [SMD]"]
  R1 = Resistor [tolerance=±1% resistance=680 package="0603 [SMD]"]
  R2 = Resistor [tolerance=±1% resistance=680 package="0603 [SMD]"]
  R3 = Resistor [tolerance=±1% resistance=330 package="0603 [SMD]"]
  C1 = Ceramic Capacitor [capacitance=220nF voltage=50V package="1206 [SMD, multilayer]"]
  C4 = Ceramic Capacitor [capacitance=100nF voltage=50V package="0603 [SMD, multilayer]"]
  C2 = Ceramic Capacitor [capacitance=220nF voltage=50V package="1206 [SMD, multilayer]"]
  C3 = Ceramic Capacitor [capacitance=1nF voltage=50V package="0603 [SMD, multilayer]"]
  out = akizuki 3.5mm Audio Jack [package=audio-jack-3.5mm]
  in = akizuki 3.5mm Audio Jack [package=audio-jack-3.5mm]
  C7 = Ceramic Capacitor [capacitance=1µF voltage=16V package="0603 [SMD, multilayer]"]
  HT82V739 = HT82V739
  C9 = Ceramic Capacitor [capacitance=1µF voltage=16V package="0603 [SMD, multilayer]"]
  SP1 = SPEAKER [package=pcb_mount_speaker]
  S1 = Toggle Switch [package=THT]
  R10 = Resistor [tolerance=±1% resistance=10k package="0603 [SMD]"]
  D5 = Pushbutton [package="[THT]"]
  D4 = Pushbutton [package="[THT]"]
  D3 = Pushbutton [package="[THT]"]
  D2 = Pushbutton [package="[THT]"]
  パーツ1 = Arduino Uno (Rev3)
  vol = Trimmer Potentiometer [package=THT]
  A1 = Trimmer Potentiometer [package=THT]
  A3 = Trimmer Potentiometer [package=THT]
  A4 = Trimmer Potentiometer [package=THT]
  A2 = Trimmer Potentiometer [package=THT]
  A5 = Trimmer Potentiometer [package=THT]
  R10k = Resistor [tolerance=±1% resistance=10k package=THT]
  R10k_2 = Resistor [tolerance=±1% resistance=10k package=THT]
  R10k_3 = Resistor [tolerance=±1% resistance=10k package=THT]
  R10k_4 = Resistor [tolerance=±1% resistance=10k package=THT]
  C6 = Ceramic Capacitor [capacitance=10µF voltage=50V package="1206 [SMD, multilayer]"]
  C8 = Ceramic Capacitor [capacitance=100µF package="1206 [SMD, multilayer]"]
  006P = Battery block 9V

nets (from the schematic view):
  5V: R6.Pin_0, HT82V739.VDD, D5.Pin_1, D5.Pin_2, D4.Pin_1, D4.Pin_2, D3.Pin_1, D3.Pin_2, D2.Pin_1, D2.Pin_2, パーツ1.5V, A1.leg2, A3.leg2, A4.leg2, A2.leg2, A5.leg2, C8.1
  N1: R6.Pin_1, R5.Pin_0, C5.0, in.LEFT, C6.0
  GND: R5.Pin_1, C5.1, R3.Pin_0, C4.1, C2.0, out.SLEEVE, in.SLEEVE, C7.0, HT82V739.VSS, HT82V739.CE, R10.Pin_1, パーツ1.GND, vol.leg1, A1.leg1, A3.leg1, A4.leg1, A2.leg1, A5.leg1, C8.0, 006P.-
  D9: R4.Pin_0, パーツ1.D9_PWM
  N2: R4.Pin_1, R1.Pin_0, C1.1, C4.0
  N3: R1.Pin_1, R2.Pin_0, C2.1
  N4: R2.Pin_1, C3.0, S1.COM
  N5: R3.Pin_1, C1.0, C3.1
  N6: out.LEFT, S1.L1
  N7: C7.1, HT82V739.VREF
  OUTN: HT82V739.OUTN, SP1.-
  N8: HT82V739.Aud_In, C9.1
  OUTP: HT82V739.OUTP, SP1.+
  N9: C9.0, vol.wiper
  N10: S1.L2, R10.Pin_0, vol.leg2
  D5: D5.Pin_3, D5.Pin_4, パーツ1.D5_PWM, R10k_4.Pin_1
  D4: D4.Pin_3, D4.Pin_4, パーツ1.D4, R10k_3.Pin_1
  D3: D3.Pin_3, D3.Pin_4, パーツ1.D3_PWM, R10k_2.Pin_1
  D2: D2.Pin_3, D2.Pin_4, パーツ1.D2, R10k.Pin_1
  A0: パーツ1.A0, C6.1
  A1: パーツ1.A1, A1.wiper
  A2: パーツ1.A2, A2.wiper
  A3: パーツ1.A3, A3.wiper
  A4: パーツ1.A4/SDA, A4.wiper
  A5: パーツ1.A5/SCL, A5.wiper
  N11: パーツ1.VIN, 006P.+
  N12: R10k.Pin_0, R10k_2.Pin_0, R10k_3.Pin_0, R10k_4.Pin_0

notes:
  in
  out
  audio
  mono audio output 3.5mm jack
  mono audio input 3.5mm jack
  D9 is default Mozzi output
  A0 is default Mozzi input
  D9 is default Mozzi output
  A0 is default Mozzi inpu
  6kHz low-pass and 16384Hz notch filter
  This circuit based on
  Notch filter for STANDARD mode carrier frequency
  (http://sensorium.github.io/Mozzi/learn/output/)
  output
  to Arduino A0 pin
  from Arduino D9 pin
  input
  www.breadboardband.org
  sp
  -
  +V
  -V
  github.com/BreadboardBand
  +
  speaker

custom parts:
  akizuki 3.5mm Audio Jack: 3.5mm Audio Jack akizuki st-005
  HT82V739: HT82V739 AMP
  SPEAKER: db-mylar-speaker-UM1515IA085008LFMP-pcb speakers.
  Arduino Uno (Rev3): The Arduino Uno is a microcontroller board based on the ATmega328 (datasheet). It has 14 digital input/output pins (of which 6 can be used as PWM outputs), 6 analog inputs, a 16 MHz ceramic resonator, a USB connection, a power jack, an ICSP header, and a reset button. It contains everything needed to support the microcontroller; simply connect it to a computer with a USB cable or power it with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
  Trimmer Potentiometer: GF063P1KB203 tokyo cosmos 6mm trimmer potentiometer.

// code stored in the sketch: Blink.ino
/*
  Blink
  Turns on an LED on for one second, then off for one second, repeatedly.
 
  This example code is in the public domain.
 */

void setup() {                
  // initialize the digital pin as an output.
  // Pin 13 has an LED connected on most Arduino boards:
  pinMode(13, OUTPUT);     
}

void loop() {
  digitalWrite(13, HIGH);   // set the LED on
  delay(1000);              // wait for a second
  digitalWrite(13, LOW);    // set the LED off
  delay(1000);              // wait for a second
}
